// Logisim project RiskVCPU.circ as structural Verilog: 1 circuit, main circuit RiskVCPU
module RiskVCPU (
  input  SysClk,
  input  Reset,
  input  PCWEn,
  input  [31:0] Instruction,
  output halt,
  output [31:0] OutTest
);

  wire ASel, BSel, ecall, MemRead, MemWrite, PCSel, RegWEn, SysClk_t;
  wire [1:0] AddrOffset, WBSel;
  wire [2:0] ImmSel, MemByteSel;
  wire [3:0] StoreMask;
  wire [4:0] ALUSel, BrSel, rdi, rs1, rs2;
  wire [31:0] ALUOut, bit_extender_1_out, bit_extender_2_out, ImmGenOut, Inst, MemInAligned, MemOut,
       MemOutAligned, MemWriteData, PC, PCPlus4, RDataA, RDataB, RegWBData;

  Clock clock_1 (.out(SysClk_t));
  // Probe on PC
  // Probe on PCPlus4
  // Probe on Inst
  IMem imem_1 (.PC(PC), .Inst(Inst));
  ProgramCounter programcounter_1 (
    .TargetAddr(ALUOut), .BranchCtl(PCSel), .PCWEn(1'b1), .Clk(SysClk_t), .Reset(1'b0), .PcOut(PC),
    .PcPlus4(PCPlus4));
  // Probe on ImmGenOut
  // Probe on RDataA
  // Probe on RDataB
  // Probe on RegWBData
  MainController maincontroller_1 (
    .Inst(Inst), .ImmSel(ImmSel), .ASel(ASel), .BSel(BSel), .ALUSel(ALUSel), .BrSel(BrSel),
    .MemRead(MemRead), .MemWrite(MemWrite), .MemByteSel(MemByteSel), .RegWEn(RegWEn), .WBSel(WBSel),
    .Is_Ecall(ecall), .Is_Ebreak(halt), .rdi(rdi), .rs1(rs1), .rs2(rs2));  // open: op_code
  ImmGen immgen_1 (.InstIn(Inst), .ImmSelIn(ImmSel), .ImmOut(ImmGenOut));
  RegisterFile registerfile_1 (
    .Data(RegWBData), .RdAddr(rdi), .Rs1Addr(rs1), .Rs2Addr(rs2), .WriteEnable(RegWEn), .Clk(SysClk_t),
    .Rs1Out(RDataA), .Rs2Out(RDataB));
  // Probe on ImmSel
  // Probe on ASel
  // Probe on BSel
  // Probe on ALUSel
  // Probe on BrSel
  // Probe on MemRead
  // Probe on MemWrite
  // Probe on MemByteSel
  // Probe on RegWEn
  // Probe on WBSel
  // Probe on ecall
  // Probe on halt
  // Probe on rdi
  // Probe on rs1
  // Probe on rs2
  // Probe on PCSel
  // Probe on ALUOut
  BranchController branchcontroller_1 (.DataA(RDataA), .DataB(RDataB), .BrSel(BrSel), .TakeBranch(PCSel));
  ALUControl alucontrol_1 (
    .RDataA(RDataA), .PC(PC), .ASel(ASel), .RDataB(RDataB), .ImmVal(ImmGenOut), .BSel(BSel), .ALUSel(ALUSel),
    .DataOut(ALUOut));
  // Probe on MemWriteData
  // Probe on RDataB
  // Probe on AddrOffset
  // Probe on MemByteSel
  // Probe on MemOut
  // Probe on MemInAligned
  // Probe on MemOutAligned
  // Probe on AddrOffset
  DMem dmem_1 (
    .AluOut(ALUOut), .MemWrite(MemWrite), .MemRead(MemRead), .StoreMast(StoreMask), .clk(SysClk_t),
    .WriteData(MemWriteData), .AddrOffset(AddrOffset), .MemOut(MemOut));
  StoreAligner storealigner_1 (
    .Data(RDataB), .AddrOffset(AddrOffset), .ByteSel(MemByteSel), .DataOut(MemWriteData), .MaskOut(StoreMask));
  LoadAligner loadaligner_1 (.AddrOffset(AddrOffset), .Data(MemOut), .ByteSel(MemByteSel), .Out0(MemOutAligned));
  // Probe on WBSel
  // Probe on RegWBData
  assign bit_extender_1_out = {{31{MemWrite}}, MemWrite};  // Bit_Extender bit_extender_1
  assign bit_extender_2_out = {{31{halt}}, halt};  // Bit_Extender bit_extender_2
  WriteBackControl writebackcontrol_1 (
    .ALUOut(ALUOut), .MemOut(MemOutAligned), .PCPlus4(PCPlus4), .WBSel(WBSel), .OutData(RegWBData));
  assign OutTest = MemWriteData & bit_extender_2_out & bit_extender_1_out;  // AND_Gate and_1, 32 bits wide

  // Other names for the same wires on the sheet: ebreak = halt

  // Notes on the sheet:
  //   IF - Instruction Fetch
  //   ID - Instruction Decode
  //   EX - Execute
  //   MEM - Memory
  //   00 = ALU
  //   01 = Mem
  //   11 = PCPlus4
  //   WB - Write Back
endmodule
